# Fritzing sketch DHHT11Uno (saved by Fritzing 0.9.3b)
breadboards: 1

parts:
  Componente2 = Arduino Uno (Rev3)
  DHT11_1 = DHT11 module

nets:
  N1: Componente2.D2, DHT11_1.DATA
  5V: Componente2.5V, DHT11_1.VCC
  GND: Componente2.GND, DHT11_1.GND

custom parts:
  DHT11 module: DHT11 black pcb module
