# Fritzing sketch DHT11ReleUno (saved by Fritzing 0.9.3b)
breadboards: 1

parts:
  KY-1 = Keyes Relay [package=THT]
  Power_plug1 = Power plug
  DHT11_1 = DHT11 module
  LED2 = LEDs [package=led10mm]
  Componente2 = Arduino Uno (Rev3)

nets:
  N1: KY-1.signal, Componente2.D8
  VCC: KY-1.power, DHT11_1.VCC, Componente2.5V
  GND: KY-1.ground, DHT11_1.GND, Componente2.GND
  N2: KY-1.C, Power_plug1.GND
  N3: KY-1.NO, LED2.C
  N4: Power_plug1.VCC, LED2.A
  N5: DHT11_1.DATA, Componente2.D2

custom parts:
  Keyes Relay: The Keyes 5V relay module is suitable for SCM development, home appliance control. It uses a 5V~12V TIL control signal which can control DC / AC signal.
  DHT11 module: DHT11 black pcb module
  LEDs: LEDs Standard schematic elements and footprints for 5mm, 3mm, 1206, and 0603 sized LEDs. 5mm - Spark Fun Electronics SKU : COM-00529 (and others)
