# Fritzing sketch JoystickUno (saved by Fritzing 0.9.3b)

parts:
  Componente2 = Arduino Uno (Rev3)
  Componente3 = Thumb Joystick

nets:
  N1: Componente2.A0, Componente3.VERT
  N2: Componente2.A1, Componente3.HORZ
  5V: Componente2.5V, Componente3.VCC
  GND: Componente2.GND, Componente3.GND
