# Fritzing sketch LDRPotServoUno (saved by Fritzing 0.9.3b)
breadboards: 1

parts:
  Componente2 = Arduino Uno (Rev3)
  R2 = Photocell (LDR) [package=THT]
  R3 = Rotary Potentiometer (Small) [maximum_resistance=100kΩ package=THT]
  J1 = Basic Servo

nets:
  N1: Componente2.A0, R2.pin_0, R3.wiper
  5V: Componente2.5V, R3.leg1, J1.vcc
  GND: Componente2.GND, R2.pin_1, J1.gnd
