# Fritzing sketch LDRUno (saved by Fritzing 0.9.3b)
breadboards: 1

parts:
  R1 = Resistor [tolerance=±5% resistance=100k package=THT]
  Componente2 = Arduino Uno (Rev3)
  R2 = Photocell (LDR) [package=THT]

nets:
  N1: R1.Pin_0, Componente2.5V
  N2: R1.Pin_1, Componente2.A0, R2.pin_0
  N3: Componente2.GND, R2.pin_1
