# Fritzing sketch LDR_3xLedsUno (saved by Fritzing 0.9.3b)
breadboards: 1

parts:
  R1 = Resistor [tolerance=±5% resistance=100k package=THT]
  Componente2 = Arduino Uno (Rev3)
  R2 = Photocell (LDR) [package=THT]
  LED1 = LED - 5mm [color="Red (633nm)" package="5 mm [THT]"]
  R3 = Resistor [tolerance=±5% resistance=220 package=THT]
  LED2 = LED - 5mm [color="Yellow (595nm)" package="5 mm [THT]"]
  R4 = Resistor [tolerance=±5% resistance=220 package=THT]
  LED3 = LED - 5mm [color="Green (560nm)" package="5 mm [THT]"]
  R5 = Resistor [tolerance=±5% resistance=220 package=THT]

nets:
  N1: R1.Pin_0, Componente2.5V
  N2: R1.Pin_1, Componente2.A0, R2.pin_0
  N3: Componente2.D11_PWM/MOSI, R5.Pin_0
  N4: Componente2.D12/MISO, R4.Pin_0
  N5: Componente2.D13/SCK, R3.Pin_0
  N6: Componente2.GND, R2.pin_1, LED1.cathode, LED2.cathode, LED3.cathode
  N7: LED1.anode, R3.Pin_1
  N8: LED2.anode, R4.Pin_1
  N9: LED3.anode, R5.Pin_1
