# Fritzing sketch RiegoReleUno (saved by Fritzing 0.9.3b)
breadboards: 1

parts:
  KY-1 = Keyes Relay [package=THT]
  Power_plug1 = Power plug
  Componente2 = Arduino Uno (Rev3)
  Componente3 = Soil Moisture Sensor
  M1 = DC Motor

nets:
  N1: KY-1.signal, Componente2.D8
  5V: KY-1.power, Componente2.5V, Componente3.VCC
  GND: KY-1.ground, Componente2.GND, Componente3.GND
  N2: KY-1.C, Power_plug1.GND
  N3: KY-1.NO, M1.pin_2
  N4: Componente2.A0, Componente3.SIG

custom parts:
  Keyes Relay: The Keyes 5V relay module is suitable for SCM development, home appliance control. It uses a 5V~12V TIL control signal which can control DC / AC signal.
